// Digital circuit 27C1024.dig as structural Verilog
module _27C1024 (
  input  nCE,
  input  nOE,
  input  VPP,
  input  VDD,
  input  GND,
  input  I_O0,
  input  I_O1,
  input  I_O2,
  input  I_O3,
  input  I_O4,
  input  I_O5,
  input  I_O6,
  input  I_O7,
  input  A0,
  input  A1,
  input  A2,
  input  A3,
  input  A4,
  input  A5,
  input  A6,
  input  A7,
  input  A8,
  input  A9,
  input  A10,
  input  A11,
  input  A12,
  input  A13,
  input  A14,
  input  A15,
  input  I_O8,
  input  I_O9,
  input  I_O10,
  input  I_O11,
  input  I_O12,
  input  I_O13,
  input  I_O14,
  input  I_O15,
  input  VSS
);

  wire nor_1_out;
  wire [15:0] U7ROM1_d;

  PowerSupply powersupply_1 (.VDD(VDD), .GND(GND));
  EEPROM #(.AddrBits(16), .isProgramMemory("true"), .Bits(16)) U7ROM1 (
    .A({A15, A14, A13, A12, A11, A10, A9, A8, A7, A6, A5, A4, A3, A2, A1, A0}), .CS(~nCE), .WE(~VPP),
    .OE(~nOE), .D(U7ROM1_d));
  nor nor_1 (nor_1_out, nCE, ~VPP, nOE);  // NOr
  BusSplitter #(.Bits(16)) bussplitter_1 (
    .D(U7ROM1_d), .OE(nor_1_out), .D0(I_O0), .D1(I_O1), .D2(I_O2), .D3(I_O3), .D4(I_O4), .D5(I_O5),
    .D6(I_O6), .D7(I_O7), .D8(I_O8), .D9(I_O9), .D10(I_O10), .D11(I_O11), .D12(I_O12), .D13(I_O13),
    .D14(I_O14), .D15(I_O15));

  assign VSS = GND;

  // Notes on the sheet:
  //   nCE: pin 2, default 1
  //   nOE: pin 20, default 1
  //   VPP: pin 1, default 1
  //   VDD: pin 40, default 1
  //   GND: pin 11
  //   I_O0: pin 19
  //   I_O1: pin 18
  //   I_O2: pin 17
  //   I_O3: pin 16
  //   I_O4: pin 15
  //   I_O5: pin 14
  //   I_O6: pin 13
  //   I_O7: pin 12
  //   A0: pin 21
  //   A1: pin 22
  //   A2: pin 23
  //   A3: pin 24
  //   A4: pin 25
  //   A5: pin 26
  //   A6: pin 27
  //   A7: pin 28
  //   A8: pin 29
  //   A9: pin 31
  //   A10: pin 32
  //   A11: pin 33
  //   A12: pin 34
  //   A13: pin 35
  //   A14: pin 36
  //   A15: pin 37
  //   I_O8: pin 10
  //   I_O9: pin 9
  //   I_O10: pin 8
  //   I_O11: pin 7
  //   I_O12: pin 6
  //   I_O13: pin 5
  //   I_O14: pin 4
  //   I_O15: pin 3
  //   VSS: pin 30
  //   contents of U7ROM1 (hex, n*v repeats v):
  //   f837,3837,ffff,3837,ffff,f837,ffff,f837,ffff,f837,ffff,f837,ffff
  //   ,3837,ffff,ffff,ffff,61bd,5*ffff,61bd,ffff,e19f,5*ffff,e19f,ffff
  //   ,46bd,5*ffff,46bd,ffff,46bb,5*ffff,46bb,ffff,c69f,5*ffff,c69f
  //   ,ffff,fff7,5*ffff,fff7,ffff,3837,ffff,f837,ffff,3837,ffff,f837
  //   ,ffff,f837,ffff,3837,ffff,f837,ffff,3837,ffff,4a7d,5*ffff,4a7d
  //   ,ffff,ca5f,5*ffff,ca5f,ffff,3837,5*ffff,3837,ffff,7836,5*ffff
  //   ,7836,ffff,447d,5*ffff,447d,ffff,c45f,4*ffff,f837,c45f
  //   contents of ROM1 (hex, n*v repeats v):
  //   c00,9118,f618,fcc1,d00,91d6,ff00,8169,cca,91c2,3669,8bec,ff00 ,9069,2bca,8161,1cf0,9101,37fc,
  //   c82,ff00,3cc2,1eec,91a0,3f01,1dec ,91a0,3d00,8018,cc18,9000,3ed2,99d6,e01,b5f4,3c8d,bf60,96c2,
  //   3701 ,2ef4,9681,f360,fc2,9981,3ec2,9801,d80,b1ec,38d2,9901,d80,b1ec ,3fd6,8300,8c18,d018,ef00,
  //   97c2,e90,9100,37d6,5ddc,dfdc,3bdc,2edc ,b5dc,fedc,cdc,91dc,ffdc,80dc,f00,95c2,ff00,8fc2,fc2,
  //   90c2,3bc2 ,d2c2,a700,ef18,ef18,a100,20c2,fc2,bcc2,3f00,8d18,d018,3fc2,1fc2 ,9114,3fe0,2fc2,
  //   d000,39c2,1200,9cc2,4314,fbca,f6ca,ffca,bdc2,3ec2 ,9200,5bc2,f700,2bc2,7fc2,8cc2,ad00,a2c2,
  //   8f00,f4c2,f900,75c2,7601 ,a3a0,5fc2,9314,45e0,fb00,3602,d02,9002,4902,8102,d02,9314,cbe0 ,f600,
  //   4f14,cfe0,f600,4b14,cbe0,ff00,9314,cbe0,f600,4714,cfe0,f600 ,4b14,cbe0,ff00,9314,ffe0,f600,
  //   4714,cfe0,f600,4b14,cbe0,ff00,9314 ,fbe0,f600,4314,cfe0,f600,4b14,cbe0,ff00,9314,ffe0,f600,
  //   4314,cfe0 ,f600,4b14,cbe0,ff00,9314,4be0,9000,4714,cfe0,f600,4b14,cbe0,ff00 ,9314,ffe0,f600,
  //   4f14,cfe0,f600,4b14,cbe0,ff00,9314,ffe0,f600,4714 ,cfe0,f600,4b14,cbe0,ff00,9314,cbe0,f600,
  //   4714,cfe0,f600,4b14,cbe0 ,ff00,d314,ebe0,f700,7314,ebe0,ff00,9314,fbe0,f600,4314,cfe0,f600 ,
  //   4b14,cbe0,ff00,9314,ffe0,f600,4314,cfe0,f600,4b14,cbe0,ff00,9314 ,ffe0,f600,5714,ede0,9b15,
  //   fb14,d5e0,1d01,9102,4202,b419,4502,f14 ,dbe0,f700,99c3,d00,19fe,fdfe,714,ebe0,fcc2,9515,ffe0,
  //   ff00,ca00 ,1fc2,9000,67c2,b300,dc2,9100,b4c2,9e81,4ec2,f61,9f61,4781,87c2 ,d81,99c2,56e8,97fc,
  //   5760,6d60,9781,47c2,ad01,1df0,9ffc,39a0,bf01 ,6dc2,2ff0,b3fc,4500,8100,2f81,b7ec,3afc,f800,
  //   6ee4,2fc2,d880,49fe ,c9fc,f00,bfc2,7efc,9421,4f00,f00,9300,4500,d200,a500,7a00,7600 ,a300,5900,
  //   8300,f00,9f00,3f00,9c00,4c00,d00,9200,4300,8300,d00 ,9900,3d00,9e00,55c2,1d00,9dc2,3e01,d3f0,
  //   7d00,1fc2,9515,ffe0,b300 ,5314,de0,9114,3b01,fb20,65c2,2d01,dcec,7dfc,9100,f900,1d41,94c2 ,
  //   3c01,f3f0,67fc,da0,9000,3ec2,9f19,4701,2d21,9180,6919,83d6,7f00 ,ff29,fe89,feca,ce30,d05,ff89,
  //   fd89,ffca,fd20,fb69,4112,fa09,4714 ,d8d,fde8,7ffc,bf20,3f00,9381,37c2,9301,5714,1f19,9901,f9f4,
  //   8380 ,dc2,bda0,bdec,9da1,4200,9ffc,9fc2,d9ec,c100,9ffc,dfc2,bf01,7302 ,7360,a1c2,5b01,df60,
  //   bfec,9bfc,4fc3,dc0,9901,4f20,a7f0,f01,b500 ,5ec2,9515,ffe0,3d00,f6fc,5f19,8f40,1d21,93c2,3fc0,
  //   bf00,5ec2,d15 ,ffe0,7b00,e7fc,1f19,bfe0,3d14,9101,ef60,bfec,9201,49a0,93c2,7f20 ,d7f0,ee00,
  //   d5fc,c5fc,d00,bfec,49a0,8102,8d00,93c2,fbfc,9002,56c2 ,d00,97c2,4b00,85c2,1d01,df60,ffec,9b01,
  //   d5e8,f01,9bc2,4d01,8bc2 ,dffc,f700,3e00,9bc2,4fc2,d02,9cc2,7d00,ddec,da0,9102,53c2,fafc ,4500,
  //   f01,9320,42c2,eb00,1fc2,9515,ffe0,b600,4b14,fd09,99c2,5fc2 ,f1ec,f3fc,7500,fc00,adc2,5a01,a121,
  //   d80,9314,b5e0,9018,4402,d02 ,fe,fdfe,416,68e2,befe,9201,cf00,8dc2,d14,9911,400d,90de,64c2 ,
  //   d0d,9f91,6015,c100,d5d,915d,385d,905d,4c5d,d5d,905d,475d,815d ,d5d,915d,395d,905d,495d,d5d,
  //   905d,4c5d,815d,d5d,915d,3d5d,905d ,495d,d5d,905d,455d,815d,d5d,915d,3d5d,905d,405d,d5d,905d,
  //   445d ,815d,d5d,915d,395d,905d,455d,d5d,815d,d5d,915d,345d,d5d,815d ,d5d,915d,2d5d,d5d,815d,
  //   d5d,905d,3d5d,915d,4c5d,d5d,905d,405d ,915d,4a5d,d5d,905d,455d,915d,495d,d05d,a15d,755d,755d,
  //   a15d,595d ,d5d,905d,405d,915d,475d,d5d,905d,3b5d,915d,455d,d5d,905d,405d ,915d,445d,d5d,905d,
  //   3d5d,915d,455d,d5d,905d,405d,915d,475d,d5d ,905d,395d,915d,495d,d5d,905d,405d,915d,455d,d5d,
  //   905d,385d,915d ,475d,d5d,905d,405d,915d,4a5d,d5d,905d,395d,915d,495d,d5d,905d ,405d,915d,4a5d,
  //   d5d,905d,455d,915d,4c5d,d5d,905d,405d,815d,d5d ,915d,445d,905d,3b5d,d5d,905d,405d,815d,d5d,
  //   915d,455d,905d,3d5d ,d5d,905d,475d,915d,405d,d5d,905d,495d,d018,a301,7721,7780,a118 ,5ad6,ff00,
  //   ff29,fd89,feca,c030,8105,ff89,fd89,ffca,fc20,fb69,d12 ,fa09,4714,818d,cde8,d5fc,7f20,bf00,3f81,
  //   fc2,9301,4dfd,c118,df00 ,9dc2,4f14,9901,3d90,1f01,908d,3bfd,9fd2,dd00,9dc2,4b01,9f40,5621 ,
  //   1fc2,93c0,3ffd,9f11,1f11,9901,eea0,f5f0,fc80,dc2,9100,5cfd,9dc2 ,3fc0,ed00,9cfd,5dc2,9114,3ce0,
  //   cd00,b001,bf80,a1d2,1f01,91a5,f4f0 ,9fc2,fefc,d00,9dc2,ff00,9fc2,d15,ffe0,7e00,fe,fdfe,416,
  //   68e2,1bfe ,9715,3d81,fe8,95c2,5e01,8380,1fd2,910d,44de,90fe,4b0d,f80,9ce4 ,49a0,d114,bfe1,7700,
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endmodule
