// Digital circuit KB165.dig as structural Verilog
module KB165 (
  input  Din,
  input  Clk,
  input  D14,
  input  D15,
  input  D12,
  input  D13,
  input  D10,
  input  D11,
  input  D8,
  input  D9,
  input  SH_nLD,
  input  D6,
  input  D7,
  input  D4,
  input  D5,
  input  D2,
  input  D3,
  input  D0,
  input  D1,
  input  VDD,
  input  GND,
  output Q14,
  output Q13,
  output Q12,
  output Q11,
  output Q10,
  output Q9,
  output Q8,
  output Q7,
  output Q15,
  output Q6,
  output Q5,
  output Q4,
  output Q3,
  output Q2,
  output Q1,
  output Q0,
  output nQ0
);

  wire nand_1_out, nand_2_out, nand_3_out, nand_4_out, nand_5_out, nand_6_out, nand_7_out, nand_9_out,
       nand_10_out, nand_11_out, nand_12_out, nand_13_out, nand_14_out, nand_15_out, nand_17_out,
       nand_18_out, nand_19_out, nand_20_out, nand_21_out, nand_22_out, nand_23_out, nand_25_out,
       nand_26_out, nand_27_out, nand_28_out, nand_29_out, nand_30_out, nand_31_out, nand_33_out,
       nand_34_out, nand_35_out, nand_36_out, nand_37_out, nand_38_out, nand_39_out, nand_41_out,
       nand_42_out, nand_43_out, nand_44_out, nand_45_out, nand_46_out, nand_47_out, nand_49_out,
       nand_50_out, nand_51_out, nand_52_out, nand_53_out, nand_54_out, nand_55_out, nand_57_out,
       nand_58_out, nand_59_out, nand_60_out, nand_61_out, nand_62_out, nand_63_out, nand_65_out,
       nand_66_out, nand_67_out, nand_68_out, nand_69_out, nand_70_out, nand_71_out, nand_73_out,
       nand_74_out, nand_75_out, nand_76_out, nand_77_out, nand_78_out, nand_79_out, nand_81_out,
       nand_82_out, nand_83_out, nand_84_out, nand_85_out, nand_86_out, nand_87_out, nand_89_out,
       nand_90_out, nand_91_out, nand_92_out, nand_93_out, nand_94_out, nand_95_out, nand_97_out,
       nand_98_out, nand_99_out, nand_100_out, nand_101_out, nand_102_out, nand_103_out, nand_105_out,
       nand_106_out, nand_107_out, nand_108_out, nand_109_out, nand_110_out, nand_111_out, nand_113_out,
       nand_114_out, nand_115_out, nand_116_out, nand_117_out, nand_118_out, nand_119_out, nand_121_out,
       nand_122_out, nand_123_out, nand_124_out, nand_125_out, nand_126_out, nand_127_out;

  nand nand_1 (nand_1_out, SH_nLD, SH_nLD);
  PowerSupply powersupply_1 (.VDD(VDD), .GND(GND));
  nand nand_2 (nand_2_out, nand_3_out, nand_1_out);
  nand nand_3 (nand_3_out, D15, nand_1_out);
  nand nand_4 (nand_4_out, nand_3_out, nand_7_out, nand_5_out);
  nand nand_5 (nand_5_out, nand_4_out, Clk, nand_2_out);
  nand nand_6 (nand_6_out, nand_5_out, Clk, nand_7_out);
  nand nand_7 (nand_7_out, nand_6_out, Din, nand_2_out);
  nand nand_8 (Q15, nand_3_out, nand_5_out, nand_9_out);
  nand nand_9 (nand_9_out, Q15, nand_6_out, nand_2_out);
  nand nand_10 (nand_10_out, D14, nand_1_out);
  nand nand_11 (nand_11_out, nand_10_out, nand_1_out);
  nand nand_12 (nand_12_out, nand_10_out, nand_15_out, nand_13_out);
  nand nand_13 (nand_13_out, nand_12_out, Clk, nand_11_out);
  nand nand_14 (nand_14_out, nand_13_out, Clk, nand_15_out);
  nand nand_15 (nand_15_out, nand_14_out, Q15, nand_11_out);
  nand nand_16 (Q14, nand_10_out, nand_13_out, nand_17_out);
  nand nand_17 (nand_17_out, Q14, nand_14_out, nand_11_out);
  nand nand_18 (nand_18_out, nand_19_out, nand_1_out);
  nand nand_19 (nand_19_out, D13, nand_1_out);
  nand nand_20 (nand_20_out, nand_19_out, nand_23_out, nand_21_out);
  nand nand_21 (nand_21_out, nand_20_out, Clk, nand_18_out);
  nand nand_22 (nand_22_out, nand_21_out, Clk, nand_23_out);
  nand nand_23 (nand_23_out, nand_22_out, Q14, nand_18_out);
  nand nand_24 (Q13, nand_19_out, nand_21_out, nand_25_out);
  nand nand_25 (nand_25_out, Q13, nand_22_out, nand_18_out);
  nand nand_26 (nand_26_out, nand_27_out, nand_1_out);
  nand nand_27 (nand_27_out, D12, nand_1_out);
  nand nand_28 (nand_28_out, nand_27_out, nand_31_out, nand_29_out);
  nand nand_29 (nand_29_out, nand_28_out, Clk, nand_26_out);
  nand nand_30 (nand_30_out, nand_29_out, Clk, nand_31_out);
  nand nand_31 (nand_31_out, nand_30_out, Q13, nand_26_out);
  nand nand_32 (Q12, nand_27_out, nand_29_out, nand_33_out);
  nand nand_33 (nand_33_out, Q12, nand_30_out, nand_26_out);
  nand nand_34 (nand_34_out, nand_35_out, nand_1_out);
  nand nand_35 (nand_35_out, D11, nand_1_out);
  nand nand_36 (nand_36_out, nand_35_out, nand_39_out, nand_37_out);
  nand nand_37 (nand_37_out, nand_36_out, Clk, nand_34_out);
  nand nand_38 (nand_38_out, nand_37_out, Clk, nand_39_out);
  nand nand_39 (nand_39_out, nand_38_out, Q12, nand_34_out);
  nand nand_40 (Q11, nand_35_out, nand_37_out, nand_41_out);
  nand nand_41 (nand_41_out, Q11, nand_38_out, nand_34_out);
  nand nand_42 (nand_42_out, D10, nand_1_out);
  nand nand_43 (nand_43_out, nand_42_out, nand_1_out);
  nand nand_44 (nand_44_out, nand_42_out, nand_47_out, nand_45_out);
  nand nand_45 (nand_45_out, nand_44_out, Clk, nand_43_out);
  nand nand_46 (nand_46_out, nand_45_out, Clk, nand_47_out);
  nand nand_47 (nand_47_out, nand_46_out, Q11, nand_43_out);
  nand nand_48 (Q10, nand_42_out, nand_45_out, nand_49_out);
  nand nand_49 (nand_49_out, Q10, nand_46_out, nand_43_out);
  nand nand_50 (nand_50_out, nand_51_out, nand_1_out);
  nand nand_51 (nand_51_out, D9, nand_1_out);
  nand nand_52 (nand_52_out, nand_51_out, nand_55_out, nand_53_out);
  nand nand_53 (nand_53_out, nand_52_out, Clk, nand_50_out);
  nand nand_54 (nand_54_out, nand_53_out, Clk, nand_55_out);
  nand nand_55 (nand_55_out, nand_54_out, Q10, nand_50_out);
  nand nand_56 (Q9, nand_51_out, nand_53_out, nand_57_out);
  nand nand_57 (nand_57_out, Q9, nand_54_out, nand_50_out);
  nand nand_58 (nand_58_out, nand_59_out, nand_1_out);
  nand nand_59 (nand_59_out, D8, nand_1_out);
  nand nand_60 (nand_60_out, nand_59_out, nand_63_out, nand_61_out);
  nand nand_61 (nand_61_out, nand_60_out, Clk, nand_58_out);
  nand nand_62 (nand_62_out, nand_61_out, Clk, nand_63_out);
  nand nand_63 (nand_63_out, nand_62_out, Q9, nand_58_out);
  nand nand_64 (Q8, nand_59_out, nand_61_out, nand_65_out);
  nand nand_65 (nand_65_out, Q8, nand_62_out, nand_58_out);
  nand nand_66 (nand_66_out, nand_67_out, nand_1_out);
  nand nand_67 (nand_67_out, D7, nand_1_out);
  nand nand_68 (nand_68_out, nand_67_out, nand_71_out, nand_69_out);
  nand nand_69 (nand_69_out, nand_68_out, Clk, nand_66_out);
  nand nand_70 (nand_70_out, nand_69_out, Clk, nand_71_out);
  nand nand_71 (nand_71_out, nand_70_out, Q8, nand_66_out);
  nand nand_72 (Q7, nand_67_out, nand_69_out, nand_73_out);
  nand nand_73 (nand_73_out, Q7, nand_70_out, nand_66_out);
  nand nand_74 (nand_74_out, nand_75_out, nand_1_out);
  nand nand_75 (nand_75_out, D6, nand_1_out);
  nand nand_76 (nand_76_out, nand_75_out, nand_79_out, nand_77_out);
  nand nand_77 (nand_77_out, nand_76_out, Clk, nand_74_out);
  nand nand_78 (nand_78_out, nand_77_out, Clk, nand_79_out);
  nand nand_79 (nand_79_out, nand_78_out, Q7, nand_74_out);
  nand nand_80 (Q6, nand_75_out, nand_77_out, nand_81_out);
  nand nand_81 (nand_81_out, Q6, nand_78_out, nand_74_out);
  nand nand_82 (nand_82_out, nand_83_out, nand_1_out);
  nand nand_83 (nand_83_out, D5, nand_1_out);
  nand nand_84 (nand_84_out, nand_83_out, nand_87_out, nand_85_out);
  nand nand_85 (nand_85_out, nand_84_out, Clk, nand_82_out);
  nand nand_86 (nand_86_out, nand_85_out, Clk, nand_87_out);
  nand nand_87 (nand_87_out, nand_86_out, Q6, nand_82_out);
  nand nand_88 (Q5, nand_83_out, nand_85_out, nand_89_out);
  nand nand_89 (nand_89_out, Q5, nand_86_out, nand_82_out);
  nand nand_90 (nand_90_out, D4, nand_1_out);
  nand nand_91 (nand_91_out, nand_90_out, nand_1_out);
  nand nand_92 (nand_92_out, nand_90_out, nand_95_out, nand_93_out);
  nand nand_93 (nand_93_out, nand_92_out, Clk, nand_91_out);
  nand nand_94 (nand_94_out, nand_93_out, Clk, nand_95_out);
  nand nand_95 (nand_95_out, nand_94_out, Q5, nand_91_out);
  nand nand_96 (Q4, nand_90_out, nand_93_out, nand_97_out);
  nand nand_97 (nand_97_out, Q4, nand_94_out, nand_91_out);
  nand nand_98 (nand_98_out, nand_99_out, nand_1_out);
  nand nand_99 (nand_99_out, D3, nand_1_out);
  nand nand_100 (nand_100_out, nand_99_out, nand_103_out, nand_101_out);
  nand nand_101 (nand_101_out, nand_100_out, Clk, nand_98_out);
  nand nand_102 (nand_102_out, nand_101_out, Clk, nand_103_out);
  nand nand_103 (nand_103_out, nand_102_out, Q4, nand_98_out);
  nand nand_104 (Q3, nand_99_out, nand_101_out, nand_105_out);
  nand nand_105 (nand_105_out, Q3, nand_102_out, nand_98_out);
  nand nand_106 (nand_106_out, nand_107_out, nand_1_out);
  nand nand_107 (nand_107_out, D2, nand_1_out);
  nand nand_108 (nand_108_out, nand_107_out, nand_111_out, nand_109_out);
  nand nand_109 (nand_109_out, nand_108_out, Clk, nand_106_out);
  nand nand_110 (nand_110_out, nand_109_out, Clk, nand_111_out);
  nand nand_111 (nand_111_out, nand_110_out, Q3, nand_106_out);
  nand nand_112 (Q2, nand_107_out, nand_109_out, nand_113_out);
  nand nand_113 (nand_113_out, Q2, nand_110_out, nand_106_out);
  nand nand_114 (nand_114_out, nand_115_out, nand_1_out);
  nand nand_115 (nand_115_out, D1, nand_1_out);
  nand nand_116 (nand_116_out, nand_115_out, nand_119_out, nand_117_out);
  nand nand_117 (nand_117_out, nand_116_out, Clk, nand_114_out);
  nand nand_118 (nand_118_out, nand_117_out, Clk, nand_119_out);
  nand nand_119 (nand_119_out, nand_118_out, Q2, nand_114_out);
  nand nand_120 (Q1, nand_115_out, nand_117_out, nand_121_out);
  nand nand_121 (nand_121_out, Q1, nand_118_out, nand_114_out);
  nand nand_122 (nand_122_out, D0, nand_1_out);
  nand nand_123 (nand_123_out, nand_122_out, nand_1_out);
  nand nand_124 (nand_124_out, nand_122_out, nand_127_out, nand_125_out);
  nand nand_125 (nand_125_out, nand_124_out, Clk, nand_123_out);
  nand nand_126 (nand_126_out, nand_125_out, Clk, nand_127_out);
  nand nand_127 (nand_127_out, nand_126_out, Q1, nand_123_out);
  nand nand_128 (Q0, nand_122_out, nand_125_out, nQ0);
  nand nand_129 (nQ0, Q0, nand_126_out, nand_123_out);

  // Notes on the sheet:
  //   Din: pin 39
  //   Clk: pin 38
  //   D14: pin 4
  //   D15: pin 3
  //   D12: pin 6
  //   D13: pin 5
  //   D10: pin 8
  //   D11: pin 7
  //   D8: pin 10
  //   D9: pin 9
  //   SH_nLD: pin 1
  //   Q14: pin 36
  //   Q13: pin 35
  //   Q12: pin 34
  //   Q11: pin 33
  //   Q10: pin 32
  //   Q9: pin 31
  //   Q8: pin 29
  //   Q7: pin 28
  //   Q15: pin 37
  //   D6: pin 13
  //   D7: pin 12
  //   D4: pin 15
  //   D5: pin 14
  //   D2: pin 17
  //   D3: pin 16
  //   D0: pin 19
  //   D1: pin 18
  //   Q6: pin 27
  //   Q5: pin 26
  //   Q4: pin 25
  //   Q3: pin 24
  //   Q2: pin 23
  //   Q1: pin 22
  //   Q0: pin 21
  //   nQ0: pin 30
  //   VDD: pin 40, default 1
  //   GND: pin 20
endmodule
