// Digital circuit KB595.dig as structural Verilog
module KB595 (
  input  I15,
  input  I14,
  input  I13,
  input  I12,
  input  I11,
  input  I10,
  input  I9,
  input  I8,
  input  I7,
  input  I6,
  input  I5,
  input  I4,
  input  I3,
  input  I2,
  input  I1,
  input  I0,
  input  SH_nLD,
  input  CLK,
  input  SI,
  input  RCLK,
  input  VDD,
  input  GND,
  input  nOE,
  output SO,
  output O15,
  output O14,
  output O13,
  output O12,
  output O11,
  output O10,
  output O9,
  output O8,
  output O7,
  output O6,
  output O5,
  output O4,
  output O3,
  output O2,
  output O1,
  output O0
);

  wire ACOE, driver_1_out, driver_3_out, driver_5_out, driver_7_out, driver_9_out, driver_11_out,
       driver_13_out, driver_15_out, driver_17_out, driver_19_out, driver_21_out, driver_23_out,
       driver_25_out, driver_27_out, driver_29_out, driver_31_out, nand_1_out, nand_2_out, nand_3_out,
       nand_4_out, nand_5_out, nand_6_out, nand_7_out, nand_8_out, nand_9_out, nand_10_out, nand_11_out,
       nand_12_out, nand_13_out, nand_14_out, nand_15_out, nand_16_out, nand_17_out, nand_18_out,
       nand_19_out, nand_20_out, nand_21_out, nand_22_out, nand_23_out, nand_24_out, nand_25_out,
       nand_26_out, nand_27_out, nand_28_out, nand_29_out, nand_30_out, nand_31_out, nand_32_out,
       nand_33_out, nand_34_out, nand_35_out, nand_36_out, nand_37_out, nand_38_out, nand_39_out,
       nand_40_out, nand_41_out, nand_42_out, nand_43_out, nand_44_out, nand_45_out, nand_46_out,
       nand_47_out, nand_48_out, nand_49_out, nand_50_out, nand_51_out, nand_52_out, nand_53_out,
       nand_54_out, nand_55_out, nand_56_out, nand_57_out, nand_58_out, nand_59_out, nand_60_out,
       nand_61_out, nand_62_out, nand_63_out, nand_64_out, nand_65_out, nand_66_out, nand_67_out,
       nand_68_out, nand_69_out, nand_70_out, nand_71_out, nand_72_out, nand_73_out, nand_74_out,
       nand_75_out, nand_76_out, nand_77_out, nand_78_out, nand_79_out, nand_80_out, nand_81_out,
       nand_82_out, nand_83_out, nand_84_out, nand_85_out, nand_86_out, nand_87_out, nand_88_out,
       nand_89_out, nand_90_out, nand_91_out, nand_92_out, nand_93_out, nand_94_out, nand_95_out,
       nand_96_out, nand_97_out, nand_98_out, nand_99_out, nand_100_out, nand_101_out, nand_102_out,
       nand_103_out, nand_104_out, nand_105_out, nand_106_out, nand_107_out, nand_108_out, nand_109_out,
       nand_110_out, nand_111_out, nand_112_out, nand_113_out, nand_114_out, nand_115_out, nand_116_out,
       nand_117_out, nand_118_out, nand_119_out, nand_120_out, nand_121_out, nand_122_out, nand_123_out,
       nand_124_out, nand_125_out, nand_126_out, nand_127_out, nand_128_out, nand_129_out, nand_130_out,
       nand_131_out, nand_132_out, nand_133_out, nand_134_out, nand_135_out, nand_136_out, nand_137_out,
       nand_138_out, nand_139_out, nand_140_out, nand_141_out, nand_142_out, nand_143_out, nand_144_out,
       nand_145_out, nand_146_out, nand_147_out, nand_148_out, nand_149_out, nand_150_out, nand_151_out,
       nand_152_out, nand_153_out, nand_154_out, nand_155_out, nand_156_out, nand_157_out, nand_158_out,
       nand_159_out, nand_160_out, nand_161_out, nand_162_out, nand_163_out, nand_164_out, nand_165_out,
       nand_166_out, nand_167_out, nand_168_out, nand_169_out, nand_170_out, nand_171_out, nand_172_out,
       nand_173_out, nand_174_out, nand_175_out, nand_176_out, nand_177_out, nand_178_out, nand_179_out,
       nand_180_out, nand_181_out, nand_182_out, nand_183_out, nand_184_out, nand_185_out, nand_186_out,
       nand_187_out, nand_188_out, nand_189_out, nand_190_out, nand_191_out, nand_192_out, nand_193_out,
       nand_194_out, nand_195_out, nand_196_out, nand_197_out, nand_198_out, nand_199_out, nand_200_out,
       nand_201_out, nand_202_out, nand_203_out, nand_204_out, nand_205_out, nand_206_out, nand_207_out,
       nand_208_out, nand_209_out, nand_210_out, nand_211_out, nand_212_out, nand_213_out, nand_214_out,
       nand_215_out, nand_216_out, nand_217_out, nand_218_out, nand_219_out, nand_220_out, nand_221_out,
       nand_224_out, nand_225_out, nAout, pulldown_1_out;

  PowerSupply powersupply_1 (.VDD(VDD), .GND(GND));
  not not_1 (ACOE, nOE);
  PullDown pulldown_1 (.out(pulldown_1_out));
  nand nand_1 (nand_1_out, SH_nLD, SH_nLD);
  nand nand_2 (nand_2_out, nand_3_out, nand_1_out);
  assign driver_1_out = pulldown_1_out ? I15 : 1'bz;  // Driver driver_1
  nand nand_3 (nand_3_out, driver_1_out, nand_1_out);
  nand nand_4 (nand_4_out, nand_3_out, nand_7_out, nand_5_out);
  nand nand_5 (nand_5_out, nand_4_out, CLK, nand_2_out);
  nand nand_6 (nand_6_out, nand_5_out, CLK, nand_7_out);
  nand nand_7 (nand_7_out, nand_6_out, SI, nand_2_out);
  nand nand_8 (nand_8_out, 1'b1, nand_11_out, nand_9_out);
  nand nand_9 (nand_9_out, nand_8_out, RCLK, SH_nLD);
  nand nand_10 (nand_10_out, nand_9_out, RCLK, nand_11_out);
  nand nand_11 (nand_11_out, nand_10_out, nand_12_out, SH_nLD);
  PullDown pulldown_2 (.out(driver_1_out));
  nand nand_12 (nand_12_out, nand_3_out, nand_5_out, nand_13_out);
  nand nand_13 (nand_13_out, nand_12_out, nand_6_out, nand_2_out);
  nand nand_14 (nand_14_out, 1'b1, nand_9_out, nand_15_out);
  nand nand_15 (nand_15_out, nand_14_out, nand_10_out, SH_nLD);
  assign O15 = ACOE ? nand_14_out : 1'bz;  // Driver driver_2
  nand nand_16 (nand_16_out, nand_17_out, nand_1_out);
  assign driver_3_out = pulldown_1_out ? I14 : 1'bz;  // Driver driver_3
  nand nand_17 (nand_17_out, driver_3_out, nand_1_out);
  nand nand_18 (nand_18_out, nand_17_out, nand_21_out, nand_19_out);
  nand nand_19 (nand_19_out, nand_18_out, CLK, nand_16_out);
  nand nand_20 (nand_20_out, nand_19_out, CLK, nand_21_out);
  nand nand_21 (nand_21_out, nand_20_out, nand_12_out, nand_16_out);
  nand nand_22 (nand_22_out, 1'b1, nand_25_out, nand_23_out);
  nand nand_23 (nand_23_out, nand_22_out, RCLK, SH_nLD);
  nand nand_24 (nand_24_out, nand_23_out, RCLK, nand_25_out);
  nand nand_25 (nand_25_out, nand_24_out, nand_26_out, SH_nLD);
  PullDown pulldown_3 (.out(driver_3_out));
  nand nand_26 (nand_26_out, nand_17_out, nand_19_out, nand_27_out);
  nand nand_27 (nand_27_out, nand_26_out, nand_20_out, nand_16_out);
  nand nand_28 (nand_28_out, 1'b1, nand_23_out, nand_29_out);
  nand nand_29 (nand_29_out, nand_28_out, nand_24_out, SH_nLD);
  assign O14 = ACOE ? nand_28_out : 1'bz;  // Driver driver_4
  assign driver_5_out = pulldown_1_out ? I13 : 1'bz;  // Driver driver_5
  nand nand_30 (nand_30_out, driver_5_out, nand_1_out);
  nand nand_31 (nand_31_out, nand_30_out, nand_1_out);
  nand nand_32 (nand_32_out, nand_30_out, nand_35_out, nand_33_out);
  nand nand_33 (nand_33_out, nand_32_out, CLK, nand_31_out);
  nand nand_34 (nand_34_out, nand_33_out, CLK, nand_35_out);
  nand nand_35 (nand_35_out, nand_34_out, nand_26_out, nand_31_out);
  nand nand_36 (nand_36_out, 1'b1, nand_39_out, nand_37_out);
  nand nand_37 (nand_37_out, nand_36_out, RCLK, SH_nLD);
  nand nand_38 (nand_38_out, nand_37_out, RCLK, nand_39_out);
  nand nand_39 (nand_39_out, nand_38_out, nand_40_out, SH_nLD);
  PullDown pulldown_4 (.out(driver_5_out));
  nand nand_40 (nand_40_out, nand_30_out, nand_33_out, nand_41_out);
  nand nand_41 (nand_41_out, nand_40_out, nand_34_out, nand_31_out);
  nand nand_42 (nand_42_out, 1'b1, nand_37_out, nand_43_out);
  nand nand_43 (nand_43_out, nand_42_out, nand_38_out, SH_nLD);
  nand nand_44 (nand_44_out, nand_45_out, nand_1_out);
  assign O13 = ACOE ? nand_42_out : 1'bz;  // Driver driver_6
  assign driver_7_out = pulldown_1_out ? I12 : 1'bz;  // Driver driver_7
  nand nand_45 (nand_45_out, driver_7_out, nand_1_out);
  nand nand_46 (nand_46_out, nand_45_out, nand_49_out, nand_47_out);
  nand nand_47 (nand_47_out, nand_46_out, CLK, nand_44_out);
  nand nand_48 (nand_48_out, nand_47_out, CLK, nand_49_out);
  nand nand_49 (nand_49_out, nand_48_out, nand_40_out, nand_44_out);
  nand nand_50 (nand_50_out, 1'b1, nand_53_out, nand_51_out);
  nand nand_51 (nand_51_out, nand_50_out, RCLK, SH_nLD);
  nand nand_52 (nand_52_out, nand_51_out, RCLK, nand_53_out);
  nand nand_53 (nand_53_out, nand_52_out, nand_54_out, SH_nLD);
  PullDown pulldown_5 (.out(driver_7_out));
  nand nand_54 (nand_54_out, nand_45_out, nand_47_out, nand_55_out);
  nand nand_55 (nand_55_out, nand_54_out, nand_48_out, nand_44_out);
  nand nand_56 (nand_56_out, 1'b1, nand_51_out, nand_57_out);
  nand nand_57 (nand_57_out, nand_56_out, nand_52_out, SH_nLD);
  assign O12 = ACOE ? nand_56_out : 1'bz;  // Driver driver_8
  nand nand_58 (nand_58_out, nand_59_out, nand_1_out);
  assign driver_9_out = pulldown_1_out ? I11 : 1'bz;  // Driver driver_9
  nand nand_59 (nand_59_out, driver_9_out, nand_1_out);
  nand nand_60 (nand_60_out, nand_59_out, nand_63_out, nand_61_out);
  nand nand_61 (nand_61_out, nand_60_out, CLK, nand_58_out);
  nand nand_62 (nand_62_out, nand_61_out, CLK, nand_63_out);
  nand nand_63 (nand_63_out, nand_62_out, nand_54_out, nand_58_out);
  nand nand_64 (nand_64_out, 1'b1, nand_67_out, nand_65_out);
  nand nand_65 (nand_65_out, nand_64_out, RCLK, SH_nLD);
  nand nand_66 (nand_66_out, nand_65_out, RCLK, nand_67_out);
  nand nand_67 (nand_67_out, nand_66_out, nand_68_out, SH_nLD);
  PullDown pulldown_6 (.out(driver_9_out));
  nand nand_68 (nand_68_out, nand_59_out, nand_61_out, nand_69_out);
  nand nand_69 (nand_69_out, nand_68_out, nand_62_out, nand_58_out);
  nand nand_70 (nand_70_out, 1'b1, nand_65_out, nand_71_out);
  nand nand_71 (nand_71_out, nand_70_out, nand_66_out, SH_nLD);
  assign O11 = ACOE ? nand_70_out : 1'bz;  // Driver driver_10
  nand nand_72 (nand_72_out, nand_73_out, nand_1_out);
  assign driver_11_out = pulldown_1_out ? I10 : 1'bz;  // Driver driver_11
  nand nand_73 (nand_73_out, driver_11_out, nand_1_out);
  nand nand_74 (nand_74_out, nand_73_out, nand_77_out, nand_75_out);
  nand nand_75 (nand_75_out, nand_74_out, CLK, nand_72_out);
  nand nand_76 (nand_76_out, nand_75_out, CLK, nand_77_out);
  nand nand_77 (nand_77_out, nand_76_out, nand_68_out, nand_72_out);
  nand nand_78 (nand_78_out, 1'b1, nand_81_out, nand_79_out);
  nand nand_79 (nand_79_out, nand_78_out, RCLK, SH_nLD);
  nand nand_80 (nand_80_out, nand_79_out, RCLK, nand_81_out);
  nand nand_81 (nand_81_out, nand_80_out, nand_82_out, SH_nLD);
  PullDown pulldown_7 (.out(driver_11_out));
  nand nand_82 (nand_82_out, nand_73_out, nand_75_out, nand_83_out);
  nand nand_83 (nand_83_out, nand_82_out, nand_76_out, nand_72_out);
  nand nand_84 (nand_84_out, 1'b1, nand_79_out, nand_85_out);
  nand nand_85 (nand_85_out, nand_84_out, nand_80_out, SH_nLD);
  assign O10 = ACOE ? nand_84_out : 1'bz;  // Driver driver_12
  assign driver_13_out = pulldown_1_out ? I9 : 1'bz;  // Driver driver_13
  nand nand_86 (nand_86_out, driver_13_out, nand_1_out);
  nand nand_87 (nand_87_out, nand_86_out, nand_1_out);
  nand nand_88 (nand_88_out, nand_86_out, nand_91_out, nand_89_out);
  nand nand_89 (nand_89_out, nand_88_out, CLK, nand_87_out);
  nand nand_90 (nand_90_out, nand_89_out, CLK, nand_91_out);
  nand nand_91 (nand_91_out, nand_90_out, nand_82_out, nand_87_out);
  nand nand_92 (nand_92_out, 1'b1, nand_95_out, nand_93_out);
  nand nand_93 (nand_93_out, nand_92_out, RCLK, SH_nLD);
  nand nand_94 (nand_94_out, nand_93_out, RCLK, nand_95_out);
  nand nand_95 (nand_95_out, nand_94_out, nand_96_out, SH_nLD);
  PullDown pulldown_8 (.out(driver_13_out));
  nand nand_96 (nand_96_out, nand_86_out, nand_89_out, nand_97_out);
  nand nand_97 (nand_97_out, nand_96_out, nand_90_out, nand_87_out);
  nand nand_98 (nand_98_out, 1'b1, nand_93_out, nand_99_out);
  nand nand_99 (nand_99_out, nand_98_out, nand_94_out, SH_nLD);
  nand nand_100 (nand_100_out, nand_101_out, nand_1_out);
  assign O9 = ACOE ? nand_98_out : 1'bz;  // Driver driver_14
  assign driver_15_out = pulldown_1_out ? I8 : 1'bz;  // Driver driver_15
  nand nand_101 (nand_101_out, driver_15_out, nand_1_out);
  nand nand_102 (nand_102_out, nand_101_out, nand_105_out, nand_103_out);
  nand nand_103 (nand_103_out, nand_102_out, CLK, nand_100_out);
  nand nand_104 (nand_104_out, nand_103_out, CLK, nand_105_out);
  nand nand_105 (nand_105_out, nand_104_out, nand_96_out, nand_100_out);
  nand nand_106 (nand_106_out, 1'b1, nand_109_out, nand_107_out);
  nand nand_107 (nand_107_out, nand_106_out, RCLK, SH_nLD);
  nand nand_108 (nand_108_out, nand_107_out, RCLK, nand_109_out);
  nand nand_109 (nand_109_out, nand_108_out, nand_110_out, SH_nLD);
  PullDown pulldown_9 (.out(driver_15_out));
  nand nand_110 (nand_110_out, nand_101_out, nand_103_out, nand_111_out);
  nand nand_111 (nand_111_out, nand_110_out, nand_104_out, nand_100_out);
  nand nand_112 (nand_112_out, 1'b1, nand_107_out, nand_113_out);
  nand nand_113 (nand_113_out, nand_112_out, nand_108_out, SH_nLD);
  assign O8 = ACOE ? nand_112_out : 1'bz;  // Driver driver_16
  nand nand_114 (nand_114_out, nand_115_out, nand_1_out);
  assign driver_17_out = pulldown_1_out ? I7 : 1'bz;  // Driver driver_17
  nand nand_115 (nand_115_out, driver_17_out, nand_1_out);
  nand nand_116 (nand_116_out, nand_115_out, nand_119_out, nand_117_out);
  nand nand_117 (nand_117_out, nand_116_out, CLK, nand_114_out);
  nand nand_118 (nand_118_out, nand_117_out, CLK, nand_119_out);
  nand nand_119 (nand_119_out, nand_118_out, nand_110_out, nand_114_out);
  nand nand_120 (nand_120_out, 1'b1, nand_123_out, nand_121_out);
  nand nand_121 (nand_121_out, nand_120_out, RCLK, SH_nLD);
  nand nand_122 (nand_122_out, nand_121_out, RCLK, nand_123_out);
  nand nand_123 (nand_123_out, nand_122_out, nand_124_out, SH_nLD);
  PullDown pulldown_10 (.out(driver_17_out));
  nand nand_124 (nand_124_out, nand_115_out, nand_117_out, nand_125_out);
  nand nand_125 (nand_125_out, nand_124_out, nand_118_out, nand_114_out);
  nand nand_126 (nand_126_out, 1'b1, nand_121_out, nand_127_out);
  nand nand_127 (nand_127_out, nand_126_out, nand_122_out, SH_nLD);
  assign O7 = ACOE ? nand_126_out : 1'bz;  // Driver driver_18
  nand nand_128 (nand_128_out, nand_129_out, nand_1_out);
  assign driver_19_out = pulldown_1_out ? I6 : 1'bz;  // Driver driver_19
  nand nand_129 (nand_129_out, driver_19_out, nand_1_out);
  nand nand_130 (nand_130_out, nand_129_out, nand_133_out, nand_131_out);
  nand nand_131 (nand_131_out, nand_130_out, CLK, nand_128_out);
  nand nand_132 (nand_132_out, nand_131_out, CLK, nand_133_out);
  nand nand_133 (nand_133_out, nand_132_out, nand_124_out, nand_128_out);
  nand nand_134 (nand_134_out, 1'b1, nand_137_out, nand_135_out);
  nand nand_135 (nand_135_out, nand_134_out, RCLK, SH_nLD);
  nand nand_136 (nand_136_out, nand_135_out, RCLK, nand_137_out);
  nand nand_137 (nand_137_out, nand_136_out, nand_138_out, SH_nLD);
  PullDown pulldown_11 (.out(driver_19_out));
  nand nand_138 (nand_138_out, nand_129_out, nand_131_out, nand_139_out);
  nand nand_139 (nand_139_out, nand_138_out, nand_132_out, nand_128_out);
  nand nand_140 (nand_140_out, 1'b1, nand_135_out, nand_141_out);
  nand nand_141 (nand_141_out, nand_140_out, nand_136_out, SH_nLD);
  assign O6 = ACOE ? nand_140_out : 1'bz;  // Driver driver_20
  nand nand_142 (nand_142_out, nand_143_out, nand_1_out);
  assign driver_21_out = pulldown_1_out ? I5 : 1'bz;  // Driver driver_21
  nand nand_143 (nand_143_out, driver_21_out, nand_1_out);
  nand nand_144 (nand_144_out, nand_143_out, nand_147_out, nand_145_out);
  nand nand_145 (nand_145_out, nand_144_out, CLK, nand_142_out);
  nand nand_146 (nand_146_out, nand_145_out, CLK, nand_147_out);
  nand nand_147 (nand_147_out, nand_146_out, nand_138_out, nand_142_out);
  nand nand_148 (nand_148_out, 1'b1, nand_151_out, nand_149_out);
  nand nand_149 (nand_149_out, nand_148_out, RCLK, SH_nLD);
  nand nand_150 (nand_150_out, nand_149_out, RCLK, nand_151_out);
  nand nand_151 (nand_151_out, nand_150_out, nand_152_out, SH_nLD);
  PullDown pulldown_12 (.out(driver_21_out));
  nand nand_152 (nand_152_out, nand_143_out, nand_145_out, nand_153_out);
  nand nand_153 (nand_153_out, nand_152_out, nand_146_out, nand_142_out);
  nand nand_154 (nand_154_out, 1'b1, nand_149_out, nand_155_out);
  nand nand_155 (nand_155_out, nand_154_out, nand_150_out, SH_nLD);
  assign O5 = ACOE ? nand_154_out : 1'bz;  // Driver driver_22
  assign driver_23_out = pulldown_1_out ? I4 : 1'bz;  // Driver driver_23
  nand nand_156 (nand_156_out, driver_23_out, nand_1_out);
  nand nand_157 (nand_157_out, nand_156_out, nand_1_out);
  nand nand_158 (nand_158_out, nand_156_out, nand_161_out, nand_159_out);
  nand nand_159 (nand_159_out, nand_158_out, CLK, nand_157_out);
  nand nand_160 (nand_160_out, nand_159_out, CLK, nand_161_out);
  nand nand_161 (nand_161_out, nand_160_out, nand_152_out, nand_157_out);
  nand nand_162 (nand_162_out, 1'b1, nand_165_out, nand_163_out);
  nand nand_163 (nand_163_out, nand_162_out, RCLK, SH_nLD);
  nand nand_164 (nand_164_out, nand_163_out, RCLK, nand_165_out);
  nand nand_165 (nand_165_out, nand_164_out, nand_166_out, SH_nLD);
  PullDown pulldown_13 (.out(driver_23_out));
  nand nand_166 (nand_166_out, nand_156_out, nand_159_out, nand_167_out);
  nand nand_167 (nand_167_out, nand_166_out, nand_160_out, nand_157_out);
  nand nand_168 (nand_168_out, 1'b1, nand_163_out, nand_169_out);
  nand nand_169 (nand_169_out, nand_168_out, nand_164_out, SH_nLD);
  nand nand_170 (nand_170_out, nand_171_out, nand_1_out);
  assign O4 = ACOE ? nand_168_out : 1'bz;  // Driver driver_24
  assign driver_25_out = pulldown_1_out ? I3 : 1'bz;  // Driver driver_25
  nand nand_171 (nand_171_out, driver_25_out, nand_1_out);
  nand nand_172 (nand_172_out, nand_171_out, nand_175_out, nand_173_out);
  nand nand_173 (nand_173_out, nand_172_out, CLK, nand_170_out);
  nand nand_174 (nand_174_out, nand_173_out, CLK, nand_175_out);
  nand nand_175 (nand_175_out, nand_174_out, nand_166_out, nand_170_out);
  nand nand_176 (nand_176_out, 1'b1, nand_179_out, nand_177_out);
  nand nand_177 (nand_177_out, nand_176_out, RCLK, SH_nLD);
  nand nand_178 (nand_178_out, nand_177_out, RCLK, nand_179_out);
  nand nand_179 (nand_179_out, nand_178_out, nand_180_out, SH_nLD);
  PullDown pulldown_14 (.out(driver_25_out));
  nand nand_180 (nand_180_out, nand_171_out, nand_173_out, nand_181_out);
  nand nand_181 (nand_181_out, nand_180_out, nand_174_out, nand_170_out);
  nand nand_182 (nand_182_out, 1'b1, nand_177_out, nand_183_out);
  nand nand_183 (nand_183_out, nand_182_out, nand_178_out, SH_nLD);
  assign O3 = ACOE ? nand_182_out : 1'bz;  // Driver driver_26
  nand nand_184 (nand_184_out, nand_185_out, nand_1_out);
  assign driver_27_out = pulldown_1_out ? I2 : 1'bz;  // Driver driver_27
  nand nand_185 (nand_185_out, driver_27_out, nand_1_out);
  nand nand_186 (nand_186_out, nand_185_out, nand_189_out, nand_187_out);
  nand nand_187 (nand_187_out, nand_186_out, CLK, nand_184_out);
  nand nand_188 (nand_188_out, nand_187_out, CLK, nand_189_out);
  nand nand_189 (nand_189_out, nand_188_out, nand_180_out, nand_184_out);
  nand nand_190 (nand_190_out, 1'b1, nand_193_out, nand_191_out);
  nand nand_191 (nand_191_out, nand_190_out, RCLK, SH_nLD);
  nand nand_192 (nand_192_out, nand_191_out, RCLK, nand_193_out);
  nand nand_193 (nand_193_out, nand_192_out, nand_194_out, SH_nLD);
  PullDown pulldown_15 (.out(driver_27_out));
  nand nand_194 (nand_194_out, nand_185_out, nand_187_out, nand_195_out);
  nand nand_195 (nand_195_out, nand_194_out, nand_188_out, nand_184_out);
  nand nand_196 (nand_196_out, 1'b1, nand_191_out, nand_197_out);
  nand nand_197 (nand_197_out, nand_196_out, nand_192_out, SH_nLD);
  assign O2 = ACOE ? nand_196_out : 1'bz;  // Driver driver_28
  nand nand_198 (nand_198_out, nand_199_out, nand_1_out);
  assign driver_29_out = pulldown_1_out ? I1 : 1'bz;  // Driver driver_29
  nand nand_199 (nand_199_out, driver_29_out, nand_1_out);
  nand nand_200 (nand_200_out, nand_199_out, nand_203_out, nand_201_out);
  nand nand_201 (nand_201_out, nand_200_out, CLK, nand_198_out);
  nand nand_202 (nand_202_out, nand_201_out, CLK, nand_203_out);
  nand nand_203 (nand_203_out, nand_202_out, nand_194_out, nand_198_out);
  nand nand_204 (nand_204_out, 1'b1, nand_207_out, nand_205_out);
  nand nand_205 (nand_205_out, nand_204_out, RCLK, SH_nLD);
  nand nand_206 (nand_206_out, nand_205_out, RCLK, nand_207_out);
  nand nand_207 (nand_207_out, nand_206_out, nand_208_out, SH_nLD);
  PullDown pulldown_16 (.out(driver_29_out));
  nand nand_208 (nand_208_out, nand_199_out, nand_201_out, nand_209_out);
  nand nand_209 (nand_209_out, nand_208_out, nand_202_out, nand_198_out);
  nand nand_210 (nand_210_out, 1'b1, nand_205_out, nand_211_out);
  nand nand_211 (nand_211_out, nand_210_out, nand_206_out, SH_nLD);
  assign O1 = ACOE ? nand_210_out : 1'bz;  // Driver driver_30
  assign driver_31_out = pulldown_1_out ? I0 : 1'bz;  // Driver driver_31
  nand nand_212 (nand_212_out, driver_31_out, nand_1_out);
  nand nand_213 (nand_213_out, nand_212_out, nand_1_out);
  nand nand_214 (nand_214_out, nand_212_out, nand_217_out, nand_215_out);
  nand nand_215 (nand_215_out, nand_214_out, CLK, nand_213_out);
  nand nand_216 (nand_216_out, nand_215_out, CLK, nand_217_out);
  nand nand_217 (nand_217_out, nand_216_out, nand_208_out, nand_213_out);
  nand nand_218 (nand_218_out, 1'b1, nand_221_out, nand_219_out);
  nand nand_219 (nand_219_out, nand_218_out, RCLK, SH_nLD);
  nand nand_220 (nand_220_out, nand_219_out, RCLK, nand_221_out);
  nand nand_221 (nand_221_out, nand_220_out, SO, SH_nLD);
  PullDown pulldown_17 (.out(driver_31_out));
  nand nand_222 (SO, nand_212_out, nand_215_out, nAout);
  nand nand_223 (nAout, SO, nand_216_out, nand_213_out);
  nand nand_224 (nand_224_out, 1'b1, nand_219_out, nand_225_out);
  nand nand_225 (nand_225_out, nand_224_out, nand_220_out, SH_nLD);
  assign O0 = ACOE ? nand_224_out : 1'bz;  // Driver driver_32

  // Other names for the same wires on the sheet: Fout = SI; GCLK = CLK; nCLR = SH_nLD

  // Notes on the sheet:
  //   SO: pin 39
  //   O15: pin 3
  //   O14: pin 4
  //   O13: pin 5
  //   O12: pin 6
  //   O11: pin 7
  //   O10: pin 8
  //   O9: pin 9
  //   O8: pin 10
  //   O7: pin 12
  //   O6: pin 13
  //   O5: pin 14
  //   O4: pin 15
  //   O3: pin 16
  //   O2: pin 17
  //   O1: pin 18
  //   O0: pin 19
  //   I15: pin 37
  //   I14: pin 36
  //   I13: pin 35
  //   I12: pin 34
  //   I11: pin 33
  //   I10: pin 32
  //   I9: pin 31
  //   I8: pin 29
  //   I7: pin 28
  //   I6: pin 27
  //   I5: pin 26
  //   I4: pin 25
  //   I3: pin 24
  //   I2: pin 23
  //   I1: pin 22
  //   I0: pin 21
  //   SH_nLD: pin 1
  //   CLK: pin 38
  //   SI: pin 2
  //   RCLK: pin 30
  //   VDD: pin 40, default 1
  //   GND: pin 11
  //   nOE: pin 20
endmodule
