// Digital circuit KB74.dig as structural Verilog
module KB74 (
  input  nRES,
  input  VCC,
  input  GND,
  input  CLK,
  output GCLK,
  output GATE,
  output Q0,
  output Q1,
  output Q2,
  output Q3,
  output RCO,
  output nT0,
  output T0,
  output nT1,
  output T1,
  output nT2,
  output T2,
  output nT3,
  output T3,
  output nCLK
);

  wire nand_1_out, nand_2_out, nand_3_out, nand_4_out, nand_5_out, nand_6_out, nand_7_out, nand_8_out,
       nand_10_out, nand_13_out, nand_14_out, nand_15_out, nand_16_out, nand_17_out, nand_18_out,
       nand_19_out, nand_20_out, nand_22_out, nand_25_out, nand_26_out, nand_27_out, nand_28_out,
       nand_30_out, nand_31_out, nand_32_out, nand_33_out, nand_34_out, nand_37_out, nand_38_out,
       nand_39_out, nand_40_out, nand_42_out, nand_43_out, nand_44_out, nand_45_out, nand_46_out, nGATE;

  PowerSupply powersupply_1 (.VDD(VCC), .GND(GND));
  nand nand_1 (nand_1_out, 1'b1, nand_4_out, nand_2_out);
  nand nand_2 (nand_2_out, nand_1_out, CLK, GATE);
  nand nand_3 (nand_3_out, nand_2_out, CLK, nand_4_out);
  nand nand_4 (nand_4_out, nand_3_out, nand_10_out, GATE);
  nand nand_5 (nand_5_out, 1'b1, nand_8_out, nand_6_out);
  nand nand_6 (nand_6_out, nand_5_out, CLK, nRES);
  nand nand_7 (nand_7_out, nand_6_out, CLK, nand_8_out);
  nand nand_8 (nand_8_out, nand_7_out, RCO, nRES);
  nand nand_9 (Q0, 1'b1, nand_2_out, nand_10_out);
  nand nand_10 (nand_10_out, Q0, nand_3_out, GATE);
  nand nand_11 (T0, 1'b1, nand_6_out, nT0);
  nand nand_12 (nT0, T0, nand_7_out, nRES);
  nand nand_13 (nand_13_out, 1'b1, nand_16_out, nand_14_out);
  nand nand_14 (nand_14_out, nand_13_out, nand_10_out, GATE);
  nand nand_15 (nand_15_out, nand_14_out, nand_10_out, nand_16_out);
  nand nand_16 (nand_16_out, nand_15_out, nand_22_out, GATE);
  nand nand_17 (nand_17_out, 1'b1, nand_20_out, nand_18_out);
  nand nand_18 (nand_18_out, nand_17_out, CLK, nRES);
  nand nand_19 (nand_19_out, nand_18_out, CLK, nand_20_out);
  nand nand_20 (nand_20_out, nand_19_out, T0, nRES);
  nand nand_21 (Q1, 1'b1, nand_14_out, nand_22_out);
  nand nand_22 (nand_22_out, Q1, nand_15_out, GATE);
  nand nand_23 (T1, 1'b1, nand_18_out, nT1);
  nand nand_24 (nT1, T1, nand_19_out, nRES);
  nand nand_25 (nand_25_out, 1'b1, nand_28_out, nand_26_out);
  nand nand_26 (nand_26_out, nand_25_out, nand_22_out, GATE);
  nand nand_27 (nand_27_out, nand_26_out, nand_22_out, nand_28_out);
  nand nand_28 (nand_28_out, nand_27_out, nand_30_out, GATE);
  nand nand_29 (Q2, 1'b1, nand_26_out, nand_30_out);
  nand nand_30 (nand_30_out, Q2, nand_27_out, GATE);
  nand nand_31 (nand_31_out, 1'b1, nand_34_out, nand_32_out);
  nand nand_32 (nand_32_out, nand_31_out, CLK, nRES);
  nand nand_33 (nand_33_out, nand_32_out, CLK, nand_34_out);
  nand nand_34 (nand_34_out, nand_33_out, T1, nRES);
  nand nand_35 (T2, 1'b1, nand_32_out, nT2);
  nand nand_36 (nT2, T2, nand_33_out, nRES);
  nand nand_37 (nand_37_out, 1'b1, nand_40_out, nand_38_out);
  nand nand_38 (nand_38_out, nand_37_out, nand_30_out, GATE);
  nand nand_39 (nand_39_out, nand_38_out, nand_30_out, nand_40_out);
  nand nand_40 (nand_40_out, nand_39_out, nand_42_out, GATE);
  nand nand_41 (Q3, 1'b1, nand_38_out, nand_42_out);
  nand nand_42 (nand_42_out, Q3, nand_39_out, GATE);
  nand nand_43 (nand_43_out, 1'b1, nand_46_out, nand_44_out);
  nand nand_44 (nand_44_out, nand_43_out, CLK, nRES);
  nand nand_45 (nand_45_out, nand_44_out, CLK, nand_46_out);
  nand nand_46 (nand_46_out, nand_45_out, T2, nRES);
  and and_1 (RCO, Q0, Q1, Q2, Q3);
  nand nand_47 (T3, 1'b1, nand_44_out, nT3);
  nand nand_48 (nT3, T3, nand_45_out, nRES);
  nand nand_49 (nCLK, CLK, CLK);
  nand nand_50 (GATE, nT3, nRES, nGATE);
  nand nand_51 (nGATE, GATE, nT0);
  nand nand_52 (GCLK, nCLK, GATE);

  // Other names for the same wires on the sheet: nRESET = nRES; RST = GATE

  // Notes on the sheet:
  //   GCLK: pin 13
  //   GATE: pin 12
  //   Q0: pin 15
  //   Q1: pin 16
  //   Q2: pin 17
  //   Q3: pin 18
  //   RCO: pin 19
  //   nT0: pin 3
  //   T0: pin 2
  //   nT1: pin 5
  //   T1: pin 4
  //   nT2: pin 7
  //   T2: pin 6
  //   nT3: pin 9
  //   T3: pin 8
  //   nRES: pin 1
  //   nCLK: pin 11
  //   VCC: pin 20, default 1
  //   GND: pin 10
  //   CLK: pin 14, Hz: 4
  //   Clock Sequencer
endmodule
