// Digital circuit KB_74_clock_seq.dig as structural Verilog
module KB_74_clock_seq (
  input  clk,
  input  in_8,
  output GCLK,
  output GATE,
  output nT0,
  output nT1,
  output nT2,
  output nT3
);

  wire Bin, BUS0, BUS1, BUS2, BUS3, BUS4, BUS5, BUS6, BUS7, BUS8, BUS9, BUS10, BUS11, BUS12, BUS13, BUS14,
       BUS15, IR0, IR1, IR2, IR3, IR4, IR5, IR6, IR7, kb74_1_nclk, MA8, MA9, MA10, MA11, MA12, MA13, MA14,
       MA15, P0, P1, P2, P3, P4, P5, P6, P7, PC0, PC1, PC2, PC3, PC4, PC5, PC6, PC7, PC8, PC9, PC10, PC11,
       PC12, PC13, PC14, PC15, reset_1_out;

  Reset reset_1 (.out(reset_1_out));
  KB74 kb74_1 (
    .GCLK(GCLK), .GATE(GATE), .nT0(nT0), .nT1(nT1), .nT2(nT2), .nT3(nT3), .nRES(reset_1_out),
    .nCLK(kb74_1_nclk), .VCC(1'b1), .GND(1'b0), .CLK(clk));  // open: Q0, Q1, Q2, Q3, RCO, T0, T1, T2, T3
  Seven_Seg_Hex seven_seg_hex_1 (.d({PC15, PC14, PC13, PC12}), .dp(1'b0));
  KB595 U3 (
    .SO(Bin), .I15(IR7), .I14(IR6), .I13(IR5), .I12(IR4), .I11(IR3), .I10(IR2), .I9(IR1), .I8(IR0), .I7(P7),
    .I6(P6), .I5(P5), .I4(P4), .I3(P3), .I2(P2), .I1(P1), .I0(P0), .CLK(GCLK), .VDD(1'b1), .GND(1'b0),
    .nOE(1'b0));  // open: O15, O14, O13, O12, O11, O10, O9, O8, O7, O6, O5, O4, O3, O2, O1, O0, SH_nLD, SI, RCLK
  Seven_Seg_Hex seven_seg_hex_2 (.d({PC11, PC10, PC9, PC8}), .dp(1'b0));
  Seven_Seg_Hex seven_seg_hex_3 (.d({PC7, PC6, PC5, PC4}), .dp(1'b0));
  Seven_Seg_Hex seven_seg_hex_4 (.d({PC3, PC2, PC1, PC0}), .dp(1'b0));
  Seven_Seg_Hex seven_seg_hex_5 (.d({IR7, IR6, IR5, IR4}), .dp(1'b0));
  Seven_Seg_Hex seven_seg_hex_6 (.d({IR3, IR2, IR1, IR0}), .dp(1'b0));
  _27C1024 U2 (
    .nCE(in_8), .nOE(1'b0), .VPP(1'b1), .VDD(1'b1), .GND(1'b0), .I_O0(P0), .I_O1(P1), .I_O2(P2), .I_O3(P3),
    .I_O4(P4), .I_O5(P5), .I_O6(P6), .I_O7(P7), .A0(PC0), .A1(PC1), .A2(PC2), .A3(PC3), .A4(PC4), .A5(PC5),
    .A6(PC6), .A7(PC7), .A8(PC8), .A9(PC9), .A10(PC10), .A11(PC11), .A12(PC12), .A13(PC13), .A14(PC14),
    .A15(PC15), .I_O8(IR0), .I_O9(IR1), .I_O10(IR2), .I_O11(IR3), .I_O12(IR4), .I_O13(IR5), .I_O14(IR6),
    .I_O15(IR7), .VSS(1'b0));
  Seven_Seg_Hex seven_seg_hex_7 (.d({P7, P6, P5, P4}), .dp(1'b0));
  Seven_Seg_Hex seven_seg_hex_8 (.d({P3, P2, P1, P0}), .dp(1'b0));
  Seven_Seg_Hex seven_seg_hex_9 (.d({MA15, MA14, MA13, MA12}), .dp(1'b0));
  Seven_Seg_Hex seven_seg_hex_10 (.d({MA11, MA10, MA9, MA8}), .dp(1'b0));
  Seven_Seg_Hex seven_seg_hex_11 (.d({P7, P6, P5, P4}), .dp(1'b0));
  Seven_Seg_Hex seven_seg_hex_12 (.d({P3, P2, P1, P0}), .dp(1'b0));
  Seven_Seg_Hex seven_seg_hex_13 (.d({BUS15, BUS14, BUS13, BUS12}), .dp(1'b0));
  Seven_Seg_Hex seven_seg_hex_14 (.d({BUS11, BUS10, BUS9, BUS8}), .dp(1'b0));
  Seven_Seg_Hex seven_seg_hex_15 (.d({BUS7, BUS6, BUS5, BUS4}), .dp(1'b0));
  Seven_Seg_Hex seven_seg_hex_16 (.d({BUS3, BUS2, BUS1, BUS0}), .dp(1'b0));

  // Notes on the sheet:
  //   clk: Hz: 2
  //   in_8: default 1
  //   ROM ADDRESS
  //   INSTR.      DATA
  //   ROM
  //   RAM ADDRESS
  //   AC / BUS
endmodule
