// Digital circuit NAND_TICK_13.dig as structural Verilog
module NAND_TICK_13 (
  input  clk,
  input  in_8,
  input  in_9,
  input  in_10,
  input  in_11,
  input  in_12,
  input  in_13,
  input  in_14,
  input  in_15,
  input  in_17,
  output GCLK,
  output GATE,
  output nT0,
  output nT1,
  output nT2,
  output nT3,
  output out_16
);

  wire Aout, B0, B1, B2, B3, B4, B5, B6, B7, B8, B9, B10, B11, B12, B13, B14, B15, Bin, Bout, BUS0, BUS1,
       BUS2, BUS3, BUS4, BUS5, BUS6, BUS7, BUS8, BUS9, BUS10, BUS11, BUS12, BUS13, BUS14, BUS15, IR0, IR1,
       IR2, IR3, IR4, IR5, IR6, IR7, kb74_1_nclk, nRESET, P0, P1, P2, P3, P4, P5, P6, P7, PC1, PC2, PC3, PC4,
       PC5, PC6, PC7, PC8, PC9, PC10, PC11, PC12, PC13, PC14, PC15, PCin, PCout, T0, T1;

  Seven_Seg_Hex seven_seg_hex_1 (.d({PC15, PC14, PC13, PC12}), .dp(1'b0));
  Seven_Seg_Hex seven_seg_hex_2 (.d({PC11, PC10, PC9, PC8}), .dp(1'b0));
  Reset reset_1 (.out(nRESET));
  Seven_Seg_Hex seven_seg_hex_3 (.d({PC7, PC6, PC5, PC4}), .dp(1'b0));
  KB74 kb74_1 (
    .GCLK(GCLK), .GATE(GATE), .nT0(nT0), .T0(T0), .nT1(nT1), .T1(T1), .nT2(nT2), .nT3(nT3), .nRES(nRESET),
    .nCLK(kb74_1_nclk), .VCC(1'b1), .GND(1'b0), .CLK(clk));  // open: Q0, Q1, Q2, Q3, RCO, T2, T3
  Seven_Seg_Hex seven_seg_hex_4 (.d({PC3, PC2, PC1, Bin}), .dp(1'b0));
  Seven_Seg_Hex seven_seg_hex_5 (.d({IR7, IR6, IR5, IR4}), .dp(1'b0));
  Seven_Seg_Hex seven_seg_hex_6 (.d({IR3, IR2, IR1, IR0}), .dp(1'b0));
  Seven_Seg_Hex seven_seg_hex_7 (.d({P7, P6, P5, P4}), .dp(1'b0));
  Seven_Seg_Hex seven_seg_hex_8 (.d({P3, P2, P1, P0}), .dp(1'b0));
  KB595 U3 (
    .SO(Bout), .O15(B15), .O14(B14), .O13(B13), .O12(B12), .O11(B11), .O10(B10), .O9(B9), .O8(B8), .O7(B7),
    .O6(B6), .O5(B5), .O4(B4), .O3(B3), .O2(B2), .O1(B1), .O0(B0), .I15(IR7), .I14(IR6), .I13(IR5),
    .I12(IR4), .I11(IR3), .I10(IR2), .I9(IR1), .I8(IR0), .I7(P7), .I6(P6), .I5(P5), .I4(P4), .I3(P3),
    .I2(P2), .I1(P1), .I0(P0), .SH_nLD(in_11), .CLK(GCLK), .SI(Bin), .RCLK(T1), .VDD(1'b1), .GND(1'b0),
    .nOE(1'b0));
  combo_1 combo_1_1 (
    .Fout(out_16), .PCin(PCin), .IR7(in_12), .IR6(in_13), .IR5(in_14), .IR4(in_15), .IR3(1'b0), .IR2(1'b0),
    .IR1(1'b0), .IR0(1'b0), .GCLK(GCLK), .nRES(nRESET), .Bout(Bout), .Aout(Aout), .T0(T0), .PCout(PCout),
    .VCC(1'b1), .GND(1'b0));  // open: ALU_Cout, Cin
  _27C1024 U2 (
    .nCE(in_8), .nOE(1'b0), .VPP(1'b1), .VDD(1'b1), .GND(1'b0), .I_O0(P0), .I_O1(P1), .I_O2(P2), .I_O3(P3),
    .I_O4(P4), .I_O5(P5), .I_O6(P6), .I_O7(P7), .A0(Bin), .A1(PC1), .A2(PC2), .A3(PC3), .A4(PC4), .A5(PC5),
    .A6(PC6), .A7(PC7), .A8(PC8), .A9(PC9), .A10(PC10), .A11(PC11), .A12(PC12), .A13(PC13), .A14(PC14),
    .A15(PC15), .I_O8(IR0), .I_O9(IR1), .I_O10(IR2), .I_O11(IR3), .I_O12(IR4), .I_O13(IR5), .I_O14(IR6),
    .I_O15(IR7), .VSS(1'b0));
  KB595 U4 (
    .SO(PCout), .O15(PC15), .O14(PC14), .O13(PC13), .O12(PC12), .O11(PC11), .O10(PC10), .O9(PC9), .O8(PC8),
    .O7(PC7), .O6(PC6), .O5(PC5), .O4(PC4), .O3(PC3), .O2(PC2), .O1(PC1), .O0(Bin), .I15(1'b0), .I14(1'b0),
    .I13(1'b0), .I12(1'b0), .I11(1'b0), .I10(1'b0), .I9(1'b0), .I8(1'b0), .I7(1'b0), .I6(1'b0), .I5(1'b0),
    .I4(1'b0), .I3(1'b0), .I2(1'b0), .I1(1'b0), .I0(1'b0), .SH_nLD(in_9), .CLK(GCLK), .SI(PCin), .RCLK(nT0),
    .VDD(1'b1), .GND(1'b0), .nOE(1'b0));
  Seven_Seg_Hex seven_seg_hex_9 (.d({B15, B14, B13, B12}), .dp(1'b0));
  Seven_Seg_Hex seven_seg_hex_10 (.d({B11, B10, B9, B8}), .dp(1'b0));
  Seven_Seg_Hex seven_seg_hex_11 (.d({B7, B6, B5, B4}), .dp(1'b0));
  Seven_Seg_Hex seven_seg_hex_12 (.d({B3, B2, B1, B0}), .dp(1'b0));
  Seven_Seg_Hex seven_seg_hex_13 (.d({BUS15, BUS14, BUS13, BUS12}), .dp(1'b0));
  KB595 U5 (
    .SO(Aout), .O15(BUS15), .O14(BUS14), .O13(BUS13), .O12(BUS12), .O11(BUS11), .O10(BUS10), .O9(BUS9),
    .O8(BUS8), .O7(BUS7), .O6(BUS6), .O5(BUS5), .O4(BUS4), .O3(BUS3), .O2(BUS2), .O1(BUS1), .O0(BUS0),
    .I15(BUS15), .I14(BUS14), .I13(BUS13), .I12(BUS12), .I11(BUS11), .I10(BUS10), .I9(BUS9), .I8(BUS8),
    .I7(BUS7), .I6(BUS6), .I5(BUS5), .I4(BUS4), .I3(BUS3), .I2(BUS2), .I1(BUS1), .I0(BUS0), .SH_nLD(in_17),
    .CLK(GCLK), .SI(out_16), .RCLK(nT0), .VDD(1'b1), .GND(1'b0), .nOE(1'b0));
  Seven_Seg_Hex seven_seg_hex_14 (.d({BUS11, BUS10, BUS9, BUS8}), .dp(1'b0));
  Seven_Seg_Hex seven_seg_hex_15 (.d({BUS7, BUS6, BUS5, BUS4}), .dp(1'b0));
  Seven_Seg_Hex seven_seg_hex_16 (.d({BUS3, BUS2, BUS1, BUS0}), .dp(1'b0));

  // Other names for the same wires on the sheet: Fout = out_16; nJMP = in_10; PC0 = Bin

  // Notes on the sheet:
  //   clk: Hz: 20
  //   in_9: default 1
  //   in_10: default 1
  //   in_11: default 1
  //   in_17: default 1
  //   B-REG
  //   ROM ADDRESS
  //   INSTR.      DATA
  //   ROM
  //   PC
  //   ACC
  //   AC / BUS
endmodule
