// Digital circuit NAND_TICK_16.dig as structural Verilog
module NAND_TICK_16 (
  input  clk,
  input  in_8,
  input  in_9,
  input  in_13,
  output GCLK,
  output GATE,
  output nT0,
  output nT1,
  output nT2,
  output nT3,
  output Fout,
  output nWE,
  output nOE
);

  wire _74540_1_pin11, _74540_1_pin12, _74540_1_pin13, _74540_1_pin14, _74540_1_pin15, _74540_1_pin16,
       _74540_1_pin17, _74540_1_pin18, Aout, B0, B1, B2, B3, B4, B5, B6, B7, B8, B9, B10, B11, B12, B13, B14,
       B15, B_J, BCC, Bin, BUS0, BUS1, BUS2, BUS3, BUS4, BUS5, BUS6, BUS7, BUS8, BUS9, BUS10, BUS11, BUS12,
       BUS13, BUS14, BUS15, IR0, IR1, IR2, IR3, IR4, IR5, IR6, IR7, JMP, kb74_1_nclk, MA0, MA1, MA2, MA3,
       MA4, MA5, MA6, MA7, MA8, MA9, MA10, MA11, MA12, MA13, MA14, nand_2_out, nand_3_out, nand_4_out,
       nand_5_out, nand_6_out, nand_7_out, nand_8_out, nand_9_out, nand_18_out, nand_19_out, nand_21_out,
       nand_22_out, nand_23_out, nand_24_out, nand_31_out, nCE, not_1_out, not_2_out, not_3_out, not_4_out,
       not_5_out, not_7_out, not_8_out, nRESET, nY0, nY1, nY2, nY3, nY4, nY5, nY6, nY7, P0, P1, P2, P3, P4,
       P5, P6, P7, PC0, PC1, PC2, PC3, PC4, PC5, PC6, PC7, PC8, PC9, PC10, PC11, PC12, PC13, PC14, PC15,
       PCin, PCout, S0, T0, T1, T2, T3, Y0, Y6, ZIN, ZOUT;

  Reset reset_1 (.out(nRESET));
  combo_1 combo_1_1 (
    .Fout(Fout), .PCin(PCin), .IR7(IR7), .IR6(IR6), .IR5(IR5), .IR4(IR4), .IR3(1'b0), .IR2(1'b0), .IR1(1'b0),
    .IR0(1'b0), .GCLK(GCLK), .nRES(nRESET), .Bout(Bin), .Aout(Aout), .T0(T0), .PCout(PCout), .VCC(1'b1),
    .GND(1'b0));  // open: ALU_Cout, Cin
  KB74 kb74_1 (
    .GCLK(GCLK), .GATE(GATE), .nT0(nT0), .T0(T0), .nT1(nT1), .T1(T1), .nT2(nT2), .T2(T2), .nT3(nT3), .T3(T3),
    .nRES(nRESET), .nCLK(kb74_1_nclk), .VCC(1'b1), .GND(1'b0), .CLK(clk));  // open: Q0, Q1, Q2, Q3, RCO
  DiodeForward diodeforward_1 (.in(BUS15), .out(ZIN));
  DiodeForward diodeforward_2 (.in(BUS14), .out(ZIN));
  DiodeForward diodeforward_3 (.in(BUS13), .out(ZIN));
  DiodeForward diodeforward_4 (.in(BUS12), .out(ZIN));
  DiodeForward diodeforward_5 (.in(BUS11), .out(ZIN));
  DiodeForward diodeforward_6 (.in(BUS10), .out(ZIN));
  DiodeForward diodeforward_7 (.in(BUS9), .out(ZIN));
  DiodeForward diodeforward_8 (.in(BUS8), .out(ZIN));
  DiodeForward diodeforward_9 (.in(BUS7), .out(ZIN));
  DiodeForward diodeforward_10 (.in(BUS6), .out(ZIN));
  DiodeForward diodeforward_11 (.in(BUS5), .out(ZIN));
  DiodeForward diodeforward_12 (.in(BUS4), .out(ZIN));
  DiodeForward diodeforward_13 (.in(BUS3), .out(ZIN));
  DiodeForward diodeforward_14 (.in(BUS2), .out(ZIN));
  DiodeForward diodeforward_15 (.in(BUS1), .out(ZIN));
  DiodeForward diodeforward_16 (.in(BUS0), .out(ZIN));
  PullDown pulldown_1 (.out(ZIN));
  nand nand_1 (ZOUT, ZIN, ZIN);
  Seven_Seg_Hex seven_seg_hex_1 (.d({IR7, IR6, IR5, IR4}), .dp(1'b0));
  _27C1024 U2 (
    .nCE(in_8), .nOE(1'b0), .VPP(1'b1), .VDD(1'b1), .GND(1'b0), .I_O0(P0), .I_O1(P1), .I_O2(P2), .I_O3(P3),
    .I_O4(P4), .I_O5(P5), .I_O6(P6), .I_O7(P7), .A0(PC0), .A1(PC1), .A2(PC2), .A3(PC3), .A4(PC4), .A5(PC5),
    .A6(PC6), .A7(PC7), .A8(PC8), .A9(PC9), .A10(PC10), .A11(PC11), .A12(PC12), .A13(PC13), .A14(PC14),
    .A15(PC15), .I_O8(IR0), .I_O9(IR1), .I_O10(IR2), .I_O11(IR3), .I_O12(IR4), .I_O13(IR5), .I_O14(IR6),
    .I_O15(IR7), .VSS(1'b0));
  Seven_Seg_Hex seven_seg_hex_2 (.d({IR3, IR2, IR1, IR0}), .dp(1'b0));
  Seven_Seg_Hex seven_seg_hex_3 (.d({P7, P6, P5, P4}), .dp(1'b0));
  nand nand_2 (nand_2_out, BUS15, BUS15);
  nand nand_3 (nand_3_out, ZOUT, ZOUT);
  not not_1 (not_1_out, IR4);
  not not_2 (not_2_out, IR5);
  not not_3 (not_3_out, IR6);
  not not_4 (not_4_out, 1'b0);
  Seven_Seg_Hex seven_seg_hex_4 (.d({P3, P2, P1, P0}), .dp(1'b0));
  nand nand_4 (nand_4_out, 1'b0, nY7, ZOUT);
  nand nand_5 (nand_5_out, IR2, nY7, nand_3_out);
  nand nand_6 (nand_6_out, IR1, nY7, ZOUT);
  nand nand_7 (nand_7_out, IR0, nY7, nand_3_out);
  nand nand_8 (nand_8_out, nand_4_out, nand_5_out);
  nand nand_9 (nand_9_out, nand_6_out, nand_7_out);
  nand nand_10 (nY0, not_1_out, not_2_out, not_3_out, not_4_out);
  nand nand_11 (nY1, IR4, not_2_out, not_3_out, not_4_out);
  nand nand_12 (nY2, not_1_out, IR5, not_3_out, not_4_out);
  nand nand_13 (nY3, IR4, IR5, not_3_out, not_4_out);
  nand nand_14 (nY4, not_1_out, not_2_out, IR6, not_4_out);
  nand nand_15 (nY5, IR4, not_2_out, IR6, not_4_out);
  nand nand_16 (nY6, not_1_out, IR5, IR6, not_4_out);
  nand nand_17 (nY7, IR4, IR5, IR6, not_4_out);
  Seven_Seg_Hex seven_seg_hex_5 (.d({PC15, PC14, PC13, PC12}), .dp(1'b0));
  KB595 U4 (
    .SO(PCout), .O15(PC15), .O14(PC14), .O13(PC13), .O12(PC12), .O11(PC11), .O10(PC10), .O9(PC9), .O8(PC8),
    .O7(PC7), .O6(PC6), .O5(PC5), .O4(PC4), .O3(PC3), .O2(PC2), .O1(PC1), .O0(PC0), .I15(1'b0), .I14(1'b0),
    .I13(1'b0), .I12(1'b0), .I11(1'b0), .I10(1'b0), .I9(1'b0), .I8(1'b0), .I7(1'b0), .I6(1'b0), .I5(1'b0),
    .I4(1'b0), .I3(1'b0), .I2(1'b0), .I1(1'b0), .I0(1'b0), .SH_nLD(nRESET), .CLK(GCLK), .SI(PCin),
    .RCLK(nT0), .VDD(1'b1), .GND(1'b0), .nOE(1'b0));
  Seven_Seg_Hex seven_seg_hex_6 (.d({PC11, PC10, PC9, PC8}), .dp(1'b0));
  nand nand_18 (nand_18_out, BUS15, nand_8_out);
  nand nand_19 (nand_19_out, nand_9_out, nand_2_out);
  Seven_Seg_Hex seven_seg_hex_7 (.d({PC7, PC6, PC5, PC4}), .dp(1'b0));
  Seven_Seg_Hex seven_seg_hex_8 (.d({PC3, PC2, PC1, PC0}), .dp(1'b0));
  nand nand_20 (BCC, nand_18_out, nand_19_out);
  not not_5 (not_5_out, IR7);
  nand nand_21 (nand_21_out, nRESET, T3, not_5_out);
  Seven_Seg_Hex seven_seg_hex_9 (.d({B15, B14, B13, B12}), .dp(1'b0));
  KB595 U3 (
    .SO(Bin), .O15(B15), .O14(B14), .O13(B13), .O12(B12), .O11(B11), .O10(B10), .O9(B9), .O8(B8), .O7(B7),
    .O6(B6), .O5(B5), .O4(B4), .O3(B3), .O2(B2), .O1(B1), .O0(B0), .I15(IR7), .I14(IR6), .I13(IR5),
    .I12(IR4), .I11(IR3), .I10(IR2), .I9(IR1), .I8(IR0), .I7(P7), .I6(P6), .I5(P5), .I4(P4), .I3(P3),
    .I2(P2), .I1(P1), .I0(P0), .SH_nLD(nand_21_out), .CLK(GCLK), .SI(Bin), .RCLK(nT0), .VDD(1'b1),
    .GND(1'b0), .nOE(1'b0));
  Seven_Seg_Hex seven_seg_hex_10 (.d({B11, B10, B9, B8}), .dp(1'b0));
  nand nand_22 (nand_22_out, JMP, IR3);
  nand nand_23 (nand_23_out, BCC, BCC);
  nand nand_24 (nand_24_out, nT3, Y0);
  nand nand_25 (nWE, T2, in_13);
  nand nand_26 (nCE, T1, Y0);
  nand nand_27 (Y0, nY0, nY0);
  nand nand_28 (Y6, nY6, nY6);
  nand nand_29 (JMP, nY7, nY7);
  nand nand_30 (S0, nCE, nCE);
  Seven_Seg_Hex seven_seg_hex_11 (.d({B7, B6, B5, B4}), .dp(1'b0));
  Seven_Seg_Hex seven_seg_hex_12 (.d({B3, B2, B1, B0}), .dp(1'b0));
  nand nand_31 (nand_31_out, nand_23_out, nY7);
  not not_6 (nOE, nand_24_out);
  nand nand_32 (B_J, nand_22_out, nand_31_out);
  not not_7 (not_7_out, GATE);
  Seven_Seg_Hex seven_seg_hex_13 (.d({BUS15, BUS14, BUS13, BUS12}), .dp(1'b0));
  KB595 U5 (
    .SO(Aout), .O15(BUS15), .O14(BUS14), .O13(BUS13), .O12(BUS12), .O11(BUS11), .O10(BUS10), .O9(BUS9),
    .O8(BUS8), .O7(BUS7), .O6(BUS6), .O5(BUS5), .O4(BUS4), .O3(BUS3), .O2(BUS2), .O1(BUS1), .O0(BUS0),
    .I15(BUS15), .I14(BUS14), .I13(BUS13), .I12(BUS12), .I11(BUS11), .I10(BUS10), .I9(BUS9), .I8(BUS8),
    .I7(BUS7), .I6(BUS6), .I5(BUS5), .I4(BUS4), .I3(BUS3), .I2(BUS2), .I1(BUS1), .I0(BUS0), .SH_nLD(nRESET),
    .CLK(GCLK), .SI(Fout), .RCLK(nT0), .VDD(1'b1), .GND(1'b0), .nOE(not_7_out));
  Seven_Seg_Hex seven_seg_hex_14 (.d({BUS11, BUS10, BUS9, BUS8}), .dp(1'b0));
  Seven_Seg_Hex seven_seg_hex_15 (.d({BUS7, BUS6, BUS5, BUS4}), .dp(1'b0));
  Seven_Seg_Hex seven_seg_hex_16 (.d({BUS3, BUS2, BUS1, BUS0}), .dp(1'b0));
  not not_8 (not_8_out, IR7);
  Seven_Seg_Hex seven_seg_hex_17 (.d({1'b0, MA14, MA13, MA12}), .dp(1'b0));
  _74541 _74541_1 (
    .pin1(not_8_out), .pin2(1'b0), .pin3(1'b0), .pin4(1'b0), .pin5(1'b0), .pin6(IR3), .pin7(IR2), .pin8(IR1),
    .pin9(IR0), .pin10(1'b0), .pin11(MA8), .pin12(MA9), .pin13(MA10), .pin14(MA11), .pin15(MA12),
    .pin16(MA13), .pin17(MA14), .pin19(not_8_out), .pin20(1'b1));  // open: pin18
  Seven_Seg_Hex seven_seg_hex_18 (.d({MA11, MA10, MA9, MA8}), .dp(1'b0));
  _74541 _74541_2 (
    .pin1(not_8_out), .pin2(P7), .pin3(P6), .pin4(P5), .pin5(P4), .pin6(P3), .pin7(P2), .pin8(P1), .pin9(P0),
    .pin10(1'b0), .pin11(MA0), .pin12(MA1), .pin13(MA2), .pin14(MA3), .pin15(MA4), .pin16(MA5), .pin17(MA6),
    .pin18(MA7), .pin19(not_8_out), .pin20(1'b1));
  Seven_Seg_Hex seven_seg_hex_19 (.d({P7, P6, P5, P4}), .dp(1'b0));
  Seven_Seg_Hex seven_seg_hex_20 (.d({P3, P2, P1, P0}), .dp(1'b0));
  _62256 _62256_1 (
    .A0(MA0), .A1(MA1), .A2(MA2), .A3(MA3), .A4(MA4), .A5(MA5), .A6(MA6), .A7(MA7), .A8(MA8), .A9(MA9),
    .A10(MA10), .A11(MA11), .A12(MA12), .nCE(nCE), .nOE(nOE), .nWE(nWE), .D0(BUS8), .D1(BUS9), .D2(BUS10),
    .D3(BUS11), .D4(BUS12), .D5(BUS13), .D6(BUS14), .D7(BUS15), .VCC(1'b1), .GND(1'b0), .A13(MA13), .A14(MA14));
  _62256 _62256_2 (
    .A0(MA0), .A1(MA1), .A2(MA2), .A3(MA3), .A4(MA4), .A5(MA5), .A6(MA6), .A7(MA7), .A8(MA8), .A9(MA9),
    .A10(MA10), .A11(MA11), .A12(MA12), .nCE(nCE), .nOE(nOE), .nWE(nWE), .D0(BUS0), .D1(BUS1), .D2(BUS2),
    .D3(BUS3), .D4(BUS4), .D5(BUS5), .D6(BUS6), .D7(BUS7), .VCC(1'b1), .GND(1'b0), .A13(MA13), .A14(MA14));
  _74540 _74540_1 (
    .pin1(1'b0), .pin2(nY0), .pin3(nY1), .pin4(nY2), .pin5(nY3), .pin6(nY4), .pin7(nY5), .pin8(nY6),
    .pin9(nY7), .pin10(1'b0), .pin11(_74540_1_pin11), .pin12(_74540_1_pin12), .pin13(_74540_1_pin13),
    .pin14(_74540_1_pin14), .pin15(_74540_1_pin15), .pin16(_74540_1_pin16), .pin17(_74540_1_pin17),
    .pin18(_74540_1_pin18), .pin19(1'b0), .pin20(1'b1));
  LED LOAD (.in(_74540_1_pin18));
  LED XOR (.in(_74540_1_pin17));
  LED AND (.in(_74540_1_pin16));
  LED OR (.in(_74540_1_pin15));
  LED ADD (.in(_74540_1_pin14));
  LED SUB (.in(_74540_1_pin13));
  LED STORE (.in(_74540_1_pin12));
  LED JUMP (.in(_74540_1_pin11));

  // Other names for the same wires on the sheet: Bout = Bin; nJMP = in_9; Y7 = JMP

  // Notes on the sheet:
  //   clk: Hz: 50
  //   in_9: default 1
  //   NANDTICK
  //   DECODE LOGIC
  //   ZERO DETECT
  //   ROM
  //   INSTR.      DATA
  //   Conditional Branch
  //   Instruction Decode
  //   3 to 8 line decoder
  //   4:1 MUX
  //   PC
  //   ROM ADDRESS
  //   B-REG
  //   Bus Access
  //   Inverters
  //   ACC
  //   AC / BUS
  //   RAM ADDRESS
endmodule
