// Digital circuit combo_1.dig as structural Verilog
module combo_1 (
  input  IR7,
  input  IR6,
  input  IR5,
  input  IR4,
  input  IR3,
  input  IR2,
  input  IR1,
  input  IR0,
  input  GCLK,
  input  nRES,
  input  Bout,
  input  Aout,
  input  T0,
  input  PCout,
  input  VCC,
  input  GND,
  output Fout,
  output ALU_Cout,
  output Cin,
  output PCin
);

  wire F, I0, I1, nand_1_out, nand_2_out, nand_3_out, nand_4_out, nand_5_out, nand_7_out, nand_9_out,
       nand_15_out, nand_16_out, nand_17_out, nand_18_out, nand_19_out, nand_20_out, nand_21_out,
       nand_22_out, nand_23_out, nand_24_out, nand_26_out, nand_27_out, nand_28_out, nand_29_out,
       nand_30_out, nand_31_out, nand_32_out, nand_33_out, nand_34_out, nand_35_out, nand_36_out,
       nand_38_out, nand_39_out, nand_40_out, nand_41_out, nand_42_out, nand_45_out, nand_46_out,
       nand_47_out, nand_48_out, nand_49_out, nand_50_out, nand_51_out, nand_52_out, nand_54_out,
       nand_56_out, nB, nCLR, nCRES, nCSET, nJMP, not_1_out, not_2_out, not_3_out, not_5_out, not_6_out, nT0,
       PC_Cin, PC_Cout;

  PowerSupply powersupply_1 (.VDD(VCC), .GND(GND));
  not not_1 (not_1_out, IR4);
  not not_2 (not_2_out, IR5);
  not not_3 (not_3_out, IR6);
  nand nand_1 (nand_1_out, not_1_out, not_2_out);
  nand nand_2 (nand_2_out, IR4, IR6);
  nand nand_3 (nand_3_out, IR4, not_2_out, IR6);
  nand nand_4 (nand_4_out, not_1_out, IR5, not_3_out);
  nand nand_5 (nand_5_out, IR4, not_2_out, not_3_out);
  nand nand_6 (I0, IR4, not_2_out, not_3_out);
  nand nand_7 (nand_7_out, not_1_out, not_2_out, not_3_out, T0);
  nand nand_8 (nCSET, IR4, not_2_out, IR6, T0);
  nand nand_9 (nand_9_out, IR4, not_2_out, IR6);
  nand nand_10 (nJMP, IR6, IR5, IR4);
  nand nand_11 (F, nand_1_out, nand_2_out);
  not not_4 (nB, nand_3_out);
  nand nand_12 (I1, nand_4_out, nand_5_out);
  not not_5 (not_5_out, nand_7_out);
  not not_6 (not_6_out, IR7);
  nand nand_13 (nCRES, nand_9_out, IR3);
  nand nand_14 (nCLR, not_5_out, not_6_out);
  nand nand_15 (nand_15_out, Aout, nand_27_out);
  nand nand_16 (nand_16_out, nB, Bout);
  nand nand_17 (nand_17_out, PCout, PC_Cin);
  nand nand_18 (nand_18_out, PCout, PC_Cin);
  nand nand_19 (nand_19_out, Aout, nand_15_out);
  nand nand_20 (nand_20_out, nand_15_out, nand_27_out);
  nand nand_21 (nand_21_out, nB, nand_16_out);
  nand nand_22 (nand_22_out, nand_16_out, Bout);
  nand nand_23 (nand_23_out, PCout, nand_17_out);
  nand nand_24 (nand_24_out, nand_17_out, PC_Cin);
  nand nand_25 (PC_Cout, nand_18_out, nand_18_out);
  nand nand_26 (nand_26_out, nand_19_out, nand_20_out);
  nand nand_27 (nand_27_out, nand_21_out, nand_22_out);
  nand nand_28 (nand_28_out, nand_23_out, nand_24_out);
  nand nand_29 (nand_29_out, nJMP, nJMP);
  nand nand_30 (nand_30_out, nand_26_out, Cin);
  nand nand_31 (nand_31_out, nand_29_out, Bout);
  nand nand_32 (nand_32_out, nJMP, nand_28_out);
  nand nand_33 (nand_33_out, nand_26_out, nand_30_out);
  nand nand_34 (nand_34_out, nand_30_out, Cin);
  nand nand_35 (nand_35_out, Cin, nand_26_out);
  nand nand_36 (nand_36_out, nand_27_out, Aout);
  nand nand_37 (PCin, nand_31_out, nand_32_out);
  nand nand_38 (nand_38_out, nand_33_out, nand_34_out);
  nand nand_39 (nand_39_out, nand_35_out, nand_36_out);
  nand nand_40 (nand_40_out, nand_38_out, I0);
  nand nand_41 (nand_41_out, I1, nand_39_out);
  nand nand_42 (nand_42_out, nand_39_out, F);
  nand nand_43 (Fout, nand_40_out, nand_41_out);
  nand nand_44 (ALU_Cout, nand_42_out, nand_42_out);
  not not_7 (nT0, T0);
  nand nand_45 (nand_45_out, nCSET, nand_48_out, nand_46_out);
  nand nand_46 (nand_46_out, nand_45_out, GCLK, nCRES);
  nand nand_47 (nand_47_out, nand_46_out, GCLK, nand_48_out);
  nand nand_48 (nand_48_out, nand_47_out, ALU_Cout, nCRES);
  nand nand_49 (nand_49_out, nT0, nand_52_out, nand_50_out);
  nand nand_50 (nand_50_out, nand_49_out, GCLK, nRES);
  nand nand_51 (nand_51_out, nand_50_out, GCLK, nand_52_out);
  nand nand_52 (nand_52_out, nand_51_out, PC_Cout, nRES);
  nand nand_53 (Cin, nCSET, nand_46_out, nand_54_out);
  nand nand_54 (nand_54_out, Cin, nand_47_out, nCRES);
  nand nand_55 (PC_Cin, nT0, nand_50_out, nand_56_out);
  nand nand_56 (nand_56_out, PC_Cin, nand_51_out, nRES);

  // Other names for the same wires on the sheet: Cout = ALU_Cout; nRESET = nRES

  // Notes on the sheet:
  //   Fout: pin 4
  //   ALU_Cout: pin 5
  //   Cin: pin 8
  //   PCin: pin 6
  //   IR7: pin 18
  //   IR6: pin 17
  //   IR5: pin 16
  //   IR4: pin 15
  //   IR3: pin 14
  //   IR2: pin 13
  //   IR1: pin 12
  //   IR0: pin 11
  //   GCLK: pin 1
  //   nRES: pin 19
  //   Bout: pin 3
  //   Aout: pin 2
  //   T0: pin 9
  //   PCout: pin 7
  //   VCC: pin 20, default 1
  //   GND: pin 10
  //   Instruction Decoder
  //   ALU-PC
  //   ALU
  //   Program Counter (Incrementer)
  //   F low will Suppress Carry
  //   Carry is  set on timeslot T0 of an operation
  //   Carry FF
  //   PC Carry FF
  //   Carry is only set before Bit 0 of an operation
  //   Any residual carry is cleared before an operation
endmodule
